# Fritzing sketch esp826612-with-522rfid-checkin-station-01 (saved by Fritzing 0.9.2b)
breadboards: 1

parts:
  Part1 = RFID-RC522-v2
  U1 = ESP8266 WiFi Module [part_number=ESP8266]
  R1 = Resistor [tolerance=±5% resistance=10k package=THT]
  S1 = Pushbutton [package=THT]
  U2 = Voltage Regulator - 5V [package="TO220 [THT]"]
  S2 = Toggle Switch [package=THT]
  R2 = Resistor [tolerance=±5% resistance=10k package=THT]
  Part2 = FTDI Basic Programmer
  LED1 = LED - 5mm [color="Red (633nm)" package="5 mm [THT]"]
  R3 = Resistor [tolerance=±5% resistance=1k package=THT]
  SW1 = PowerSwitch Tail II
  R4 = Resistor [tolerance=±5% resistance=1k package=THT]
  R5 = Resistor [tolerance=±5% resistance=10k package=THT]
  R6 = Resistor [tolerance=±5% resistance=10k package=THT]
  R7 = Resistor [tolerance=±5% resistance=10k package=THT]

nets:
  N1: Part1.SDA, U1.GPIO_15, R5.Pin_1
  N2: Part1.SCK, U1.GPIO_14
  N3: Part1.MOSI, U1.GPIO_13
  N4: Part1.MISO, U1.GPIO_12
  GND: Part1.GND, U1.GND, R1.Pin_1, U2.GND, S2.L1, Part2.GND, LED1.cathode, SW1.-in, R5.Pin_0, R7.Pin_0
  N5: Part1.RST, U1.GPIO_5
  N6: Part1.3_3V, U1.VCC, U2.output_voltage, R6.Pin_0
  N7: U1.RXD, Part2.TXO
  N8: U1.GPIO_0, R2.Pin_0
  N9: U1.GPIO_2, R7.Pin_1
  N10: U1.CH_PD, R6.Pin_1
  N11: U1.TXD, Part2.RXI
  N12: U1.GPIO_4, R3.Pin_0
  N13: U1.GPIO_16, R4.Pin_0
  N14: U1.REST, S1.leg1
  N15: R1.Pin_0, S1.leg0
  N16: S2.COM, R2.Pin_1
  N17: LED1.anode, R3.Pin_1
  N18: SW1.+in, R4.Pin_1

notes:
  ESP8266 Parts from: https://github.com/ydonnelly/ESP8266_fritzing
  switch to GND for programming
  Push to reset
  RFID-RC522 Parts from: https://github.com/miguelbalboa/rfid
  PowerTail Switch Part from: https://github.com/adafruit/Fritzing-Library

custom parts:
  RFID-RC522-v2: A simple China made RFID-RC522 Reader; do check the pin labels, as this is a MFRC522 based clone.
  ESP8266 WiFi Module: Generic WiFi Module based on the ESP8266 with onboard PCB antenna and UART communications
